# Fritzing sketch Circuit's Sketch (saved by Fritzing 0.9.3b)
breadboards: 1

parts:
  Parça2 = Arduino Uno (Rev3)
  LCD2 = LCD screen
  R1_(Ekran)1 = Rotary Potentiometer (Small) [maximum_resistance=100kΩ package=THT]

nets:
  N1: Parça2.D11_PWM/MOSI, LCD2.E
  N2: Parça2.D12/MISO, LCD2.RS
  N3: Parça2.D2, LCD2.DB7
  N4: Parça2.D3_PWM, LCD2.DB6
  N5: Parça2.D4, LCD2.DB5
  N6: Parça2.D5_PWM, LCD2.DB4
  5V: Parça2.5V, LCD2.VDD, LCD2.LED+, R1_(Ekran)1.leg1
  GND: Parça2.GND, LCD2.VSS, LCD2.R/W, LCD2.LED-, R1_(Ekran)1.leg2
  N7: LCD2.V0, R1_(Ekran)1.wiper
